# Fritzing sketch arduino-breadboard (saved by Fritzing 0.9.0b)
breadboards: 1

parts:
  Arduino_Uno = Arduino Uno (Rev3)
  MAX232 = RS232 Transceiver [package=dil16]
  C232_3 = Electrolytic Capacitor [capacitance=10µF package="100 mil [THT, electrolytic]"]
  C232_1 = Electrolytic Capacitor [capacitance=10µF package="100 mil [THT, electrolytic]"]
  C232_2 = Electrolytic Capacitor [capacitance=10µF package="100 mil [THT, electrolytic]"]
  C232_4 = Electrolytic Capacitor [capacitance=10µF package="100 mil [THT, electrolytic]"]
  D-SUB = DB9 Connector [package=db9]
  Q1 = NPN-Transistor [package="TO92 [THT]"]
  R7 = Resistor [tolerance=±5% resistance=1k package=THT]
  R8 = Resistor [tolerance=±5% resistance=1k package=THT]
  V1 = DC Power [voltage=30V]

nets (from the schematic view):
  N1: Arduino_Uno.D8, MAX232.T2IN
  N2: Arduino_Uno.D9_PWM, MAX232.R2OUT
  N3: Arduino_Uno.GND, Q1.E, V1.V-
  N4: Arduino_Uno.D2, R7.Pin_0
  5V: Arduino_Uno.5V, MAX232.VCC, C232_2.-
  N5: MAX232.C1+, C232_1.-
  N6: MAX232.V+, C232_2.+
  N7: MAX232.C1-, C232_1.+
  N8: MAX232.C2+, C232_3.-
  N9: MAX232.C2-, C232_3.+
  N10: MAX232.V-, C232_4.-
  N11: MAX232.T2OUT, D-SUB.3
  N12: MAX232.R2IN, D-SUB.2
  N13: MAX232.GND, C232_4.+, D-SUB.5
  N14: Q1.B, R7.Pin_1
  N15: Q1.C, R8.Pin_1
  N16: R8.Pin_0, V1.V+

notes:
  oven rs232
